// Logisim project Main.circ as structural Verilog
module registerBank (
  input  [2:0] regLdS,
  input  [2:0] DBSel
);

  wire decoder_1_out0, decoder_1_out1, decoder_1_out2, decoder_1_out3, decoder_1_out4, decoder_1_out5;
  wire [6:0] AR_q, PC_q, SP_q;
  wire [9:0] IR_2_q, IR_q, multiplexer_10_out, RR_q;

  Decoder #(.select(3)) decoder_1 (
    .out0(decoder_1_out0), .out1(decoder_1_out1), .out2(decoder_1_out2), .out3(decoder_1_out3),
    .out4(decoder_1_out4), .out5(decoder_1_out5), .sel(regLdS), .en(1'b1));  // open: out6, out7
  Register #(.width(7)) AR (.en(decoder_1_out0), .Q(AR_q));  // open: D, clk, clr
  Register #(.width(7)) PC (.en(decoder_1_out1), .Q(PC_q));  // open: D, clk, clr
  Register #(.width(7)) SP (.en(decoder_1_out2), .Q(SP_q));  // open: D, clk, clr
  Register #(.width(10)) RR (.D(multiplexer_10_out), .en(decoder_1_out3), .Q(RR_q));  // open: clk, clr
  Register #(.width(10)) IR (.D(multiplexer_10_out), .en(decoder_1_out4), .Q(IR_q));  // open: clk, clr
  Register #(.width(10)) IR_2 (.D(multiplexer_10_out), .en(decoder_1_out5), .Q(IR_2_q));  // open: clk, clr
  RAM #(.addrWidth(12), .dataWidth(16), .bus("separate")) ram_1 ();  // open: addr, din, data, str, sel, clk, ld, clr
  Multiplexer #(.select(3)) multiplexer_1 (
    .in2(IR_2_q[9]), .in3(IR_q[9]), .in4(RR_q[9]), .out(multiplexer_10_out[9]), .sel(DBSel), .en(1'b1));  // open: in0, in1, in5, in6, in7
  Multiplexer #(.select(3)) multiplexer_2 (
    .in2(IR_2_q[8]), .in3(IR_q[8]), .in4(RR_q[8]), .out(multiplexer_10_out[8]), .sel(DBSel), .en(1'b1));  // open: in0, in1, in5, in6, in7
  Multiplexer #(.select(3)) multiplexer_3 (
    .in2(IR_2_q[7]), .in3(IR_q[7]), .in4(RR_q[7]), .out(multiplexer_10_out[7]), .sel(DBSel), .en(1'b1));  // open: in0, in1, in5, in6, in7
  Multiplexer #(.select(3)) multiplexer_4 (
    .in2(IR_2_q[6]), .in3(IR_q[6]), .in4(RR_q[6]), .in5(SP_q[6]), .in6(PC_q[6]), .in7(AR_q[6]),
    .out(multiplexer_10_out[6]), .sel(DBSel), .en(1'b1));  // open: in0, in1
  Multiplexer #(.select(3)) multiplexer_5 (
    .in2(IR_2_q[5]), .in3(IR_q[5]), .in4(RR_q[5]), .in5(SP_q[5]), .in6(PC_q[5]), .in7(AR_q[5]),
    .out(multiplexer_10_out[5]), .sel(DBSel), .en(1'b1));  // open: in0, in1
  Multiplexer #(.select(3)) multiplexer_6 (
    .in2(IR_2_q[4]), .in3(IR_q[4]), .in4(RR_q[4]), .in5(SP_q[4]), .in6(PC_q[4]), .in7(AR_q[4]),
    .out(multiplexer_10_out[4]), .sel(DBSel), .en(1'b1));  // open: in0, in1
  Multiplexer #(.select(3)) multiplexer_7 (
    .in2(IR_2_q[3]), .in3(IR_q[3]), .in4(RR_q[3]), .in5(SP_q[3]), .in6(PC_q[3]), .in7(AR_q[3]),
    .out(multiplexer_10_out[3]), .sel(DBSel), .en(1'b1));  // open: in0, in1
  Multiplexer #(.select(3)) multiplexer_8 (
    .in2(IR_2_q[2]), .in3(IR_q[2]), .in4(RR_q[2]), .in5(SP_q[2]), .in6(PC_q[2]), .in7(AR_q[2]),
    .out(multiplexer_10_out[2]), .sel(DBSel), .en(1'b1));  // open: in0, in1
  Multiplexer #(.select(3)) multiplexer_9 (
    .in2(IR_2_q[1]), .in3(IR_q[1]), .in4(RR_q[1]), .in5(SP_q[1]), .in6(PC_q[1]), .in7(AR_q[1]),
    .out(multiplexer_10_out[1]), .sel(DBSel), .en(1'b1));  // open: in0, in1
  Multiplexer #(.select(3)) multiplexer_10 (
    .in2(IR_2_q[0]), .in3(IR_q[0]), .in4(RR_q[0]), .in5(SP_q[0]), .in6(PC_q[0]), .in7(AR_q[0]),
    .out(multiplexer_10_out[0]), .sel(DBSel), .en(1'b1));  // open: in0, in1
endmodule
